# Fritzing sketch Arduino (saved by Fritzing 0.9.3b)
breadboards: 1

parts:
  Componente2 = Arduino Uno (Rev3) - ICSP
  LED4 = smd LED [color="Green (570nm)" package="1206 [SMD]"]
  LED5 = smd LED [color="Red (633nm)" package="1206 [SMD]"]
  LED6 = smd LED [color="Green (570nm)" package="1206 [SMD]"]
  R4 = Resistor [tolerance=±5% resistance=220 package=THT]
  R5 = Resistor [tolerance=±5% resistance=220 package=THT]
  R6 = Resistor [tolerance=±5% resistance=220 package=THT]
  Componente3 = HC-SR04 Ultrasonic Rangemeter  # not connected
  J2 = Basic Servo
  BT2 = Bluetooth HC-06u [package=THT]

nets:
  N1: Componente2.D12/MISO, LED6.anode
  N2: Componente2.D13/SCK, LED5.anode
  N3: Componente2.D2, BT2.TXD
  N4: Componente2.D4, BT2.RXD
  N5: Componente2.D5_PWM, LED4.anode
  N6: Componente2.D6_PWM, J2.pulse
  VCC: Componente2.5V, J2.vcc, BT2.VCC
  GND: Componente2.GND, R4.Pin_0, R5.Pin_0, R6.Pin_0, J2.gnd, BT2.GND
  N7: LED4.cathode, R5.Pin_1
  N8: LED5.cathode, R6.Pin_1
  N9: LED6.cathode, R4.Pin_1

custom parts:
  Bluetooth HC-06u: Bluetooth HC-06 - face up, pins down 16.5mm x 37.5mm PCB
